// Logisim project alu.circ as structural Verilog: 1 circuit, main circuit alu
module alu (
  input  [31:0] A,
  input  [31:0] B,
  input  [3:0] ALUSel,
  output [31:0] Result
);

  wire adder_2_cout, adder_4_cout, adder_6_cout, adder_8_cout, comparator_1_lt, S14, undriven, undriven_2,
       undriven_4, undriven_6, undriven_7, undriven_8, undriven_9;
  wire [31:0] add0, adder_6_out, adder_8_out, and1, ARet14, ARev14, bit_extender_2_out, BRet14, BRev14,
       divu8, mul10, mulh14, mulhu11, multiplier_3_cout, multiplier_3_out, multiplier_5_cout,
       multiplier_5_out, or2, remu9, sll6, slt7, sra5, srl4, sub12, undriven_3, undriven_5, xor3, xor_2_out,
       xor_6_out, xor_8_out, xor_10_out;

  Adder #(.width(32)) adder_1 (.a(A), .b(B), .out(add0));  // open: cin, cout
  Shifter #(.width(32), .shift("lr")) shifter_1 (.in(A), .\dist (B[4:0]), .out(srl4));
  Shifter #(.width(32), .shift("ar")) shifter_2 (.in(A), .\dist (B[4:0]), .out(sra5));
  Shifter #(.width(32)) shifter_3 (.in(A), .\dist (B[4:0]), .out(sll6));
  Comparator #(.width(32)) comparator_1 (.a(A), .b(B), .lt(comparator_1_lt));  // open: gt, eq
  Divider #(.width(32)) divider_1 (.a(A), .b(B), .out(divu8));  // open: upper, rem
  Divider #(.width(32)) divider_2 (.a(A), .b(B), .rem(remu9));  // open: out, upper
  Subtractor #(.width(32)) subtractor_1 (.a(A), .b(B), .out(sub12));  // open: bin, bout
  assign and1 = A & B;  // AND_Gate and_1, 32 bits wide
  assign or2 = A | B;  // OR_Gate or_1, 32 bits wide
  assign xor3 = A ^ B;  // XOR_Gate xor_1, 32 bits wide
  assign slt7 = {{31{1'b0}}, comparator_1_lt};  // Bit_Extender bit_extender_1
  Multiplier #(.width(32)) multiplier_1 (.a(A), .b(B), .out(mul10));  // open: cin, cout
  Multiplier #(.width(32)) multiplier_2 (.a(A), .b(B), .cout(mulhu11));  // open: out, cin
  Multiplexer #(.width(32)) multiplexer_1 (.in0(A), .in1(ARev14), .out(ARet14), .sel(A[31]), .en(undriven));
  Multiplexer #(.width(32)) multiplexer_2 (.in0(A), .in1(ARev14), .out(ARet14), .sel(A[31]), .en(undriven));
  assign xor_2_out = A ^ {32{1'b1}};  // XOR_Gate xor_2, 32 bits wide
  assign xor_2_out = A ^ {32{1'b1}};  // XOR_Gate xor_3, 32 bits wide
  Adder #(.width(32)) adder_2 (.a(xor_2_out), .b(32'h1), .out(ARev14), .cin(undriven_2), .cout(adder_2_cout));
  Adder #(.width(32)) adder_3 (.a(xor_2_out), .b(32'h1), .out(ARev14), .cin(undriven_2), .cout(adder_2_cout));
  xor xor_4 (S14, B[31], A[31]);
  xor xor_5 (S14, B[31], A[31]);
  Multiplier #(.width(32)) multiplier_3 (
    .a(ARet14), .b(BRet14), .out(multiplier_3_out), .cin(undriven_3), .cout(multiplier_3_cout));
  Multiplier #(.width(32)) multiplier_4 (
    .a(ARet14), .b(BRet14), .out(multiplier_3_out), .cin(undriven_3), .cout(multiplier_3_cout));
  Multiplexer #(.width(32)) multiplexer_3 (.in0(B), .in1(BRev14), .out(BRet14), .sel(B[31]), .en(undriven_4));
  Multiplexer #(.width(32)) multiplexer_4 (.in0(B), .in1(BRev14), .out(BRet14), .sel(B[31]), .en(undriven_4));
  assign xor_6_out = B ^ {32{1'b1}};  // XOR_Gate xor_6, 32 bits wide
  assign xor_6_out = B ^ {32{1'b1}};  // XOR_Gate xor_7, 32 bits wide
  Multiplier #(.width(32)) multiplier_5 (
    .a(ARet14), .b(BRet14), .out(multiplier_5_out), .cin(undriven_5), .cout(multiplier_5_cout));
  Multiplier #(.width(32)) multiplier_6 (
    .a(ARet14), .b(BRet14), .out(multiplier_5_out), .cin(undriven_5), .cout(multiplier_5_cout));
  assign xor_8_out = multiplier_3_out ^ {32{1'b1}};  // XOR_Gate xor_8, 32 bits wide
  assign xor_8_out = multiplier_3_out ^ {32{1'b1}};  // XOR_Gate xor_9, 32 bits wide
  assign xor_10_out = multiplier_3_cout ^ {32{1'b1}};  // XOR_Gate xor_10, 32 bits wide
  assign xor_10_out = multiplier_3_cout ^ {32{1'b1}};  // XOR_Gate xor_11, 32 bits wide
  Adder #(.width(32)) adder_4 (.a(xor_6_out), .b(32'h1), .out(BRev14), .cin(undriven_7), .cout(adder_4_cout));
  Adder #(.width(32)) adder_5 (.a(xor_6_out), .b(32'h1), .out(BRev14), .cin(undriven_7), .cout(adder_4_cout));
  Adder #(.width(32)) adder_6 (.a(xor_8_out), .b(32'h1), .out(adder_6_out), .cin(undriven_6), .cout(adder_6_cout));
  Adder #(.width(32)) adder_7 (.a(xor_8_out), .b(32'h1), .out(adder_6_out), .cin(undriven_6), .cout(adder_6_cout));
  assign bit_extender_2_out = {{31{1'b0}}, adder_6_cout};  // Bit_Extender bit_extender_2
  Multiplexer #(.width(32)) multiplexer_5 (
    .in0(multiplier_5_cout), .in1(adder_8_out), .out(mulh14), .sel(S14), .en(undriven_8));
  Multiplexer #(.width(32)) multiplexer_6 (
    .in0(multiplier_5_cout), .in1(adder_8_out), .out(mulh14), .sel(S14), .en(undriven_8));
  Adder #(.width(32)) adder_8 (
    .a(bit_extender_2_out), .b(xor_10_out), .out(adder_8_out), .cin(undriven_9), .cout(adder_8_cout));
  Adder #(.width(32)) adder_9 (
    .a(bit_extender_2_out), .b(xor_10_out), .out(adder_8_out), .cin(undriven_9), .cout(adder_8_cout));
  Multiplexer #(.select(4), .width(32)) multiplexer_7 (
    .in0(add0), .in1(and1), .in2(or2), .in3(xor3), .in4(srl4), .in5(sra5), .in6(sll6), .in7(slt7),
    .in8(divu8), .in9(remu9), .in10(mul10), .in11(mulhu11), .in12(sub12), .in13(B), .in14(mulh14),
    .out(Result), .sel(ALUSel));  // open: in15, en

  // Other names for the same wires on the sheet: Asel14 = A[31]; BSel13[31:0] = B; Bsel14 = B[31]

  // Notes on the sheet:
  //   INPUTS to your circuit
  //   DON'T CHANGE THE LOCATIONS OF THE INPUTS AND OUTPUTS!
  //   OUTPUT from your circuit
endmodule
