// Logisim project control_logic.circ as structural Verilog: 1 circuit, main circuit control_logic
module control_logic (
  input  [31:0] inst,
  input  BrEq,
  input  BrLt,
  output PCSel,
  output RegWEn,
  output [2:0] ImmSel,
  output BrUn,
  output ASel,
  output BSel,
  output [3:0] ALUSel,
  output MemRW,
  output [1:0] WBSel
);

  wire and_2_out, and_3_out, and_4_out, and_5_out, and_9_out, and_10_out, and_11_out, and_12_out, BRight,
       comparator_1_eq, comparator_11_eq, comparator_12_eq, comparator_13_eq, comparator_14_eq,
       comparator_15_eq, comparator_16_eq, comparator_17_eq, comparator_18_eq, comparator_19_eq,
       comparator_20_eq, comparator_21_eq, comparator_22_eq, comparator_23_eq, comparator_24_eq,
       comparator_25_eq, comparator_26_eq, comparator_27_eq, IFORMAT, IFORMAT01, IFORMAT02, IFORMAT03,
       multiplexer_1_out, multiplexer_2_out, nor_1_out, nor_2_out, not_1_out, not_2_out, or_2_out, or_3_out,
       or_4_out, or_5_out, or_7_out, or_9_out, or_10_out, or_13_out, or_14_out, or_15_out, or_16_out,
       or_17_out, or_18_out, or_19_out, or_20_out, or_21_out, or_22_out, or_23_out, or_24_out, or_26_out,
       RFORMAT, SBFORMAT, SFORMAT, UFORMAT, UFORMAT01, UFORMAT02, UJFORMAT, xor_1_out, xor_2_out;
  wire [1:0] IFORMAT02Sit, multiplexer_8_out, Order, OriSit;
  wire [3:0] multiplexer_5_out;

  Comparator #(.width(3)) comparator_1 (.a(inst[14:12]), .b(3'b110), .eq(comparator_1_eq));  // open: gt, lt
  Comparator #(.width(7)) comparator_2 (.a(inst[6:0]), .b(7'b0110011), .eq(RFORMAT));  // open: gt, lt
  Comparator #(.width(7)) comparator_3 (.a(inst[6:0]), .b(7'b0000011), .eq(IFORMAT01));  // open: gt, lt
  Comparator #(.width(7)) comparator_4 (.a(inst[6:0]), .b(7'b0010011), .eq(IFORMAT02));  // open: gt, lt
  Comparator #(.width(7)) comparator_5 (.a(inst[6:0]), .b(7'b1100111), .eq(IFORMAT03));  // open: gt, lt
  Comparator #(.width(7)) comparator_6 (.a(inst[6:0]), .b(7'b0100011), .eq(SFORMAT));  // open: gt, lt
  Comparator #(.width(7)) comparator_7 (.a(inst[6:0]), .b(7'b1100011), .eq(SBFORMAT));  // open: gt, lt
  Comparator #(.width(7)) comparator_8 (.a(inst[6:0]), .b(7'b0010111), .eq(UFORMAT01));  // open: gt, lt
  Comparator #(.width(7)) comparator_9 (.a(inst[6:0]), .b(7'b0110111), .eq(UFORMAT02));  // open: gt, lt
  Comparator #(.width(7)) comparator_10 (.a(inst[6:0]), .b(7'b1101111), .eq(UJFORMAT));  // open: gt, lt
  or or_1 (ImmSel[1], SFORMAT, SBFORMAT);
  Comparator #(.width(3)) comparator_11 (.a(inst[14:12]), .b(3'b111), .eq(comparator_11_eq));  // open: gt, lt
  or or_2 (or_2_out, IFORMAT03, UJFORMAT);
  or or_3 (or_3_out, RFORMAT, IFORMAT02);
  or or_4 (or_4_out, UFORMAT, IFORMAT01);
  or or_5 (or_5_out, IFORMAT02, IFORMAT03);
  or or_6 (UFORMAT, UFORMAT01, UFORMAT02);
  or or_7 (or_7_out, IFORMAT, SBFORMAT);
  or or_8 (ImmSel[2], UFORMAT, UJFORMAT);
  or or_9 (or_9_out, comparator_1_eq, comparator_11_eq);
  or or_10 (or_10_out, or_3_out, or_4_out);
  or or_11 (IFORMAT, IFORMAT01, or_5_out);
  or or_12 (ImmSel[0], or_7_out, UJFORMAT);
  or or_13 (or_13_out, or_2_out, IFORMAT01);
  or or_14 (or_14_out, RFORMAT, IFORMAT02);
  and and_1 (BrUn, SBFORMAT, or_9_out);
  Multiplexer #(.enable("false")) multiplexer_1 (.in1(1'b0), .out(multiplexer_1_out), .sel(or_13_out));  // open: in0
  or or_15 (or_15_out, or_14_out, UFORMAT);
  Multiplexer #(.enable("false")) multiplexer_2 (.in1(1'b0), .out(multiplexer_2_out), .sel(or_10_out));  // open: in0
  or or_16 (or_16_out, IFORMAT03, UJFORMAT);
  Multiplexer #(.enable("false")) multiplexer_3 (.in0(multiplexer_1_out), .in1(1'b1), .out(WBSel[0]), .sel(or_15_out));
  Multiplexer #(.enable("false")) multiplexer_4 (.in0(multiplexer_2_out), .in1(1'b1), .out(WBSel[1]), .sel(or_16_out));
  Comparator #(.width(3)) comparator_12 (.a(inst[14:12]), .b(3'b111), .eq(comparator_12_eq));  // open: gt, lt
  Comparator #(.width(3)) comparator_13 (.a(inst[14:12]), .b(3'b000), .eq(comparator_13_eq));  // open: gt, lt
  Comparator #(.width(3)) comparator_14 (.a(inst[14:12]), .b(3'b001), .eq(comparator_14_eq));  // open: gt, lt
  not not_1 (not_1_out, BrEq);
  Comparator #(.width(3)) comparator_15 (.a(inst[14:12]), .b(3'b101), .eq(comparator_15_eq));  // open: gt, lt
  Comparator #(.width(3)) comparator_16 (.a(inst[14:12]), .b(3'b100), .eq(comparator_16_eq));  // open: gt, lt
  Comparator #(.width(3)) comparator_17 (.a(inst[14:12]), .b(3'b110), .eq(comparator_17_eq));  // open: gt, lt
  Comparator #(.width(7)) comparator_18 (.a(inst[31:25]), .b({7{1'b0}}), .eq(comparator_18_eq));  // open: gt, lt
  Comparator #(.width(7)) comparator_19 (.a(inst[31:25]), .b(7'b0000001), .eq(comparator_19_eq));  // open: gt, lt
  Comparator #(.width(7)) comparator_20 (.a(inst[31:25]), .b(7'b0100000), .eq(comparator_20_eq));  // open: gt, lt
  Comparator #(.width(7)) comparator_21 (.a(inst[31:25]), .b(7'b0000011), .eq(comparator_21_eq));  // open: gt, lt
  Multiplexer #(.select(5), .width(4), .enable("false")) multiplexer_5 (
    .in0(4'b0000), .in1(4'b1010), .in2(4'b1100), .in4(4'b0110), .in5(4'b1110), .in8(4'b0111), .in15(4'b1011),
    .in16(4'b0011), .in20(4'b0100), .in21(4'b1000), .in22(4'b0101), .in24(4'b0010), .in28(4'b0001),
    .in29(4'b1001), .out(multiplexer_5_out), .sel({inst[14:12], Order}));  // open: in3, in6, in7, in9, in10, in11, in12, in13, in14, in17, in18, in19, in23, in25, in26, in27, in30, in31
  and and_2 (and_2_out, comparator_13_eq, BrEq);
  and and_3 (and_3_out, comparator_14_eq, not_1_out);
  or or_17 (or_17_out, comparator_15_eq, comparator_12_eq);
  Multiplexer #(.width(4), .enable("false")) multiplexer_6 (
    .in0(4'b0000), .in1(multiplexer_5_out), .out(ALUSel), .sel(or_19_out));
  not not_2 (not_2_out, BrLt);
  or or_18 (or_18_out, comparator_16_eq, comparator_17_eq);
  nor nor_1 (nor_1_out, comparator_18_eq, comparator_19_eq);
  xor xor_1 (xor_1_out, comparator_19_eq, comparator_21_eq);
  xor xor_2 (xor_2_out, comparator_20_eq, comparator_21_eq);
  nor nor_2 (nor_2_out, comparator_18_eq, comparator_20_eq);
  or or_19 (or_19_out, IFORMAT02, RFORMAT);
  and and_4 (and_4_out, or_17_out, not_2_out);
  and and_5 (and_5_out, or_18_out, BrLt);
  and and_6 (OriSit[1], nor_1_out, xor_2_out);
  and and_7 (OriSit[0], xor_1_out, nor_2_out);
  Multiplexer #(.width(2), .enable("false")) multiplexer_7 (
    .in0(IFORMAT02Sit), .in1(OriSit), .out(Order), .sel(RFORMAT));
  or or_20 (or_20_out, and_2_out, and_3_out);
  or or_21 (or_21_out, and_4_out, and_5_out);
  or or_22 (or_22_out, or_20_out, or_21_out);
  and and_8 (BRight, or_22_out, SBFORMAT);
  Comparator #(.width(3)) comparator_22 (.a(inst[14:12]), .b(3'b101), .eq(comparator_22_eq));  // open: gt, lt
  Comparator #(.width(3)) comparator_23 (.a(inst[14:12]), .b(3'b001), .eq(comparator_23_eq));  // open: gt, lt
  Comparator #(.width(3)) comparator_24 (.a(inst[14:12]), .b(3'b101), .eq(comparator_24_eq));  // open: gt, lt
  Comparator #(.width(7)) comparator_25 (.a(inst[31:25]), .b(7'b0100000), .eq(comparator_25_eq));  // open: gt, lt
  or or_23 (or_23_out, comparator_22_eq, comparator_23_eq);
  and and_9 (and_9_out, comparator_24_eq, comparator_25_eq);
  Comparator #(.width(7)) comparator_26 (.a(inst[31:25]), .b({7{1'b0}}), .eq(comparator_26_eq));  // open: gt, lt
  and and_10 (and_10_out, IFORMAT02, or_23_out);
  Multiplexer #(.width(2), .enable("false")) multiplexer_8 (
    .in0(2'b00), .in1(2'b10), .out(multiplexer_8_out), .sel(and_11_out));
  and and_11 (and_11_out, and_9_out, IFORMAT02);
  Multiplexer #(.width(2), .enable("false")) multiplexer_9 (
    .in0(multiplexer_8_out), .in1(2'b00), .out(IFORMAT02Sit), .sel(and_12_out));
  and and_12 (and_12_out, comparator_26_eq, and_10_out);
  Comparator #(.width(3)) comparator_27 (.a(inst[14:12]), .b(3'b010), .eq(comparator_27_eq));  // open: gt, lt
  not not_3 (BSel, RFORMAT);
  or or_24 (or_24_out, BRight, UJFORMAT);
  and and_13 (MemRW, SFORMAT, comparator_27_eq);
  or or_25 (PCSel, or_24_out, IFORMAT03);
  nor nor_3 (RegWEn, SFORMAT, SBFORMAT);
  or or_26 (or_26_out, SBFORMAT, UFORMAT01);
  or or_27 (ASel, or_26_out, UJFORMAT);

  // Other names for the same wires on the sheet: Opcode[6:0] = inst[6:0]; Func7[6:0] = inst[31:25];
  //   Func3[2:0] = inst[14:12]; Order[4:2] = inst[14:12]

  // Notes on the sheet:
  //   INPUTS to your circuit
  //   Immsel
  //   BASE
  //   DON'T CHANGE THE LOCATIONS OF THE INPUTS AND OUTPUTS!
  //   OUTPUT from your circuit
  //   ALU
  //   是否是Shift类的
endmodule
