// Logisim project cpu.circ as structural Verilog: 1 circuit, main circuit main
module main (
  input  [31:0] INSTRUCTION,
  input  CLOCK,
  output [31:0] PROGRAM_COUNTER,
  output [31:0] ra,
  output [31:0] sp,
  output [31:0] t0,
  output [31:0] t1,
  output [31:0] t2,
  output [31:0] s0,
  output [31:0] s1,
  output [31:0] a0
);

  wire branch_comp_1_breq, branch_comp_1_brlt, CheckAllow, comparator_5_eq, comparator_6_eq,
       control_logic_1_asel, control_logic_1_brun, control_logic_1_bsel, control_logic_1_memrw,
       control_logic_1_regwen, HalfWordCheck, LSel, multiplexer_10_out, not_1_out, not_2_out, PCSpecial,
       Right, Second, SwltCheck, undriven, undriven_2, WordCheck;
  wire [1:0] control_logic_1_wbsel, Pos;
  wire [2:0] control_logic_1_immsel;
  wire [3:0] control_logic_1_alusel;
  wire [7:0] multiplexer_5_out;
  wire [15:0] multiplexer_6_out;
  wire [31:0] adder_1_out, bit_extender_1_out, bit_extender_2_out, demultiplexer_1_out0,
       demultiplexer_1_out1, demultiplexer_1_out2, demultiplexer_1_out3, demultiplexer_2_out0,
       demultiplexer_2_out1, demultiplexer_3_out0, divider_2_rem, DMEM_p6, GetData, GetImm, INSTRUCTIONAllow,
       LoadObs, LoadOpt, LoadRet, multiplexer_1_out, multiplexer_3_out, multiplexer_4_out, multiplexer_8_out,
       multiplexer_9_out, multiplexer_11_out, NewLocal, NormalLocal, PCLocal, RegFile_read_data_1,
       register_2_q, Ret;
  wire [31:2] divider_1_rem;

  control_logic control_logic_1 (
    .BSel(control_logic_1_bsel), .BrUn(control_logic_1_brun), .RegWEn(control_logic_1_regwen),
    .ImmSel(control_logic_1_immsel), .ASel(control_logic_1_asel), .PCSel(PCSpecial),
    .BrLt(branch_comp_1_brlt), .BrEq(branch_comp_1_breq), .inst(LoadObs), .ALUSel(control_logic_1_alusel),
    .MemRW(control_logic_1_memrw), .WBSel(control_logic_1_wbsel));
  Adder #(.width(32)) adder_1 (.a(PROGRAM_COUNTER), .b(32'h4), .out(adder_1_out));  // open: cin, cout
  Multiplexer #(.width(32), .enable("false")) multiplexer_1 (
    .in0(adder_1_out), .in1(NewLocal), .out(multiplexer_1_out), .sel(PCSpecial));
  Register #(.width(32)) PC (.D(multiplexer_1_out), .en(1'b1), .clk(CLOCK), .Q(PROGRAM_COUNTER), .clr(undriven_2));
  Register #(.width(32)) instF (.D(INSTRUCTIONAllow), .en(1'b1), .clk(CLOCK), .Q(LoadObs), .clr(undriven));
  Register #(.width(32)) register_1 (.D(PROGRAM_COUNTER), .en(1'b1), .clk(not_1_out), .Q(PCLocal));  // open: clr
  not not_1 (not_1_out, CLOCK);
  Comparator #(.width(7)) comparator_1 (.a(7'b0000011), .b(LoadObs[6:0]), .eq(LSel));  // open: gt, lt
  Divider #(.width(32)) divider_1 (.a(GetImm), .b(32'h4), .rem({divider_1_rem, Pos}));  // open: out, upper
  Divider #(.width(32)) divider_2 (.a(GetImm), .b(32'h2), .rem(divider_2_rem));  // open: out, upper
  Multiplexer #(.width(32), .enable("false")) multiplexer_2 (
    .in0(INSTRUCTION), .in1({32{1'b0}}), .out(INSTRUCTIONAllow), .sel(PCSpecial));
  Comparator #(.width(32)) comparator_2 (.a({divider_1_rem, Pos}), .b(32'h2), .eq(Second));  // open: gt, lt
  Comparator #(.width(32)) comparator_3 (.a({divider_1_rem, Pos}), .b({32{1'b0}}), .eq(WordCheck));  // open: gt, lt
  Comparator #(.width(32)) comparator_4 (.a(divider_2_rem), .b({32{1'b0}}), .eq(HalfWordCheck));  // open: gt, lt
  imm_gen imm_gen_1 (.ImmSel(control_logic_1_immsel), .imm(GetImm), .inst(LoadObs));
  Demultiplexer #(.select(2), .width(32), .enable("false")) demultiplexer_1 (
    .out0(demultiplexer_1_out0), .out1(demultiplexer_1_out1), .out2(demultiplexer_1_out2),
    .out3(demultiplexer_1_out3), .in(LoadOpt), .sel(Pos));
  Multiplexer #(.width(32), .enable("false")) multiplexer_3 (
    .in1(LoadOpt), .out(multiplexer_3_out), .sel(HalfWordCheck));  // open: in0
  Demultiplexer #(.width(32), .enable("false")) demultiplexer_2 (
    .out0(demultiplexer_2_out0), .out1(demultiplexer_2_out1), .in(multiplexer_3_out), .sel(Second));
  Multiplexer #(.width(32), .enable("false")) multiplexer_4 (
    .in1(LoadOpt), .out(multiplexer_4_out), .sel(WordCheck));  // open: in0
  Multiplexer #(.select(2), .width(8), .enable("false")) multiplexer_5 (
    .in0(demultiplexer_1_out0[7:0]), .in1(demultiplexer_1_out1[15:8]), .in2(demultiplexer_1_out2[23:16]),
    .in3(demultiplexer_1_out3[31:24]), .out(multiplexer_5_out), .sel(Pos));
  Multiplexer #(.width(16), .enable("false")) multiplexer_6 (
    .in0(demultiplexer_2_out0[15:0]), .in1(demultiplexer_2_out1[31:16]), .out(multiplexer_6_out), .sel(Second));
  assign bit_extender_1_out = {{24{multiplexer_5_out[7]}}, multiplexer_5_out};  // Bit_Extender bit_extender_1
  assign bit_extender_2_out = {{16{multiplexer_6_out[15]}}, multiplexer_6_out};  // Bit_Extender bit_extender_2
  Register #(.width(32)) register_2 (.D(PCLocal), .en(1'b1), .clk(CLOCK), .Q(register_2_q));  // open: clr
  regfile_main RegFile (
    .rs2(LoadObs[24:20]), .rd(LoadObs[11:7]), .Read_Data_1(RegFile_read_data_1), .Read_Data_2(GetData),
    .ra(ra), .sp(sp), .t0(t0), .t1(t1), .t2(t2), .s0(s0), .s1(s1), .a0(a0), .rs1(LoadObs[19:15]),
    .Write_Data(Ret), .RegWEn(control_logic_1_regwen), .clk(CLOCK));
  Multiplexer #(.select(2), .width(32), .enable("false")) multiplexer_7 (
    .in0(bit_extender_1_out), .in1(bit_extender_2_out), .in2(multiplexer_4_out), .out(LoadRet),
    .sel(LoadObs[13:12]));  // open: in3
  branch_comp branch_comp_1 (
    .BrEq(branch_comp_1_breq), .rs1(RegFile_read_data_1), .rs2(GetData), .BrLt(branch_comp_1_brlt),
    .BrUn(control_logic_1_brun));
  Multiplexer #(.width(32), .enable("false")) multiplexer_8 (
    .in0(RegFile_read_data_1), .in1(register_2_q), .out(multiplexer_8_out), .sel(control_logic_1_asel));
  Adder #(.width(32)) adder_2 (.a(register_2_q), .b(32'h4), .out(NormalLocal));  // open: cin, cout
  Multiplexer #(.width(32), .enable("false")) multiplexer_9 (
    .in0(GetData), .in1(GetImm), .out(multiplexer_9_out), .sel(control_logic_1_bsel));
  alu Arithmetic_Logic_Unit (
    .Result(NewLocal), .ALUSel(control_logic_1_alusel), .A(multiplexer_8_out), .B(multiplexer_9_out));
  not not_2 (not_2_out, SwltCheck);
  Multiplexer #(.enable("false")) multiplexer_10 (
    .in1(control_logic_1_memrw), .out(multiplexer_10_out), .sel(Right));  // open: in0
  Comparator #(.width(7)) comparator_5 (.a(7'b0100011), .b(LoadObs[6:0]), .eq(comparator_5_eq));  // open: gt, lt
  Comparator #(.width(3)) comparator_6 (.a(LoadObs[14:12]), .b(3'b111), .eq(comparator_6_eq));  // open: gt, lt
  Comparator #(.width(32)) comparator_7 (.a(GetData), .b(GetImm), .lt(CheckAllow));  // open: gt, eq
  or or_1 (Right, not_2_out, CheckAllow);
  and and_1 (SwltCheck, comparator_5_eq, comparator_6_eq);
  // mem_main DMEM: pin names not known; wires that end beside it: control_logic_1_memrw, NewLocal, GetData, CLOCK, multiplexer_10_out, DMEM_p6
  Demultiplexer #(.width(32), .enable("false")) demultiplexer_3 (
    .out0(demultiplexer_3_out0), .out1(LoadOpt), .in(DMEM_p6), .sel(LSel));
  Multiplexer #(.width(32), .enable("false")) multiplexer_11 (
    .in0(demultiplexer_3_out0), .in1(LoadRet), .out(multiplexer_11_out), .sel(LSel));
  Multiplexer #(.select(2), .width(32), .enable("false")) multiplexer_12 (
    .in0(multiplexer_11_out), .in1(NewLocal), .in2(NormalLocal), .out(Ret), .sel(control_logic_1_wbsel));  // open: in3

  // Other names for the same wires on the sheet: clk = CLOCK; StoreObs[31:0] = LoadObs; LoadSel[1:0] = LoadObs[13:12]

  // Notes on the sheet:
  //   Output
  //   IMEM (do **NOT** move this)
  //   Inputs
  //   It is OK to move the PC, RegFile, ALU, MEM, Branch Comp, Imm Gen, and Control Logic to wherever is most convenient for you when constructing your CPU, and to delete this text
  //   LControl
  //   Inputs/Outputs for testing. Do **NOT** move these.
  //   ALU_Data
  //   swltControl
endmodule
